// Logisim project cpu.circ as structural Verilog: 22 circuits, main circuit d-latch
module d_latch (
  input  enabler,
  input  \input ,
  output Q,
  output Q_prime
);

  wire and_1_out, and_2_out, not_1_out;

  not not_1 (not_1_out, \input );
  and and_1 (and_1_out, not_1_out, enabler);
  and and_2 (and_2_out, enabler, \input );
  nor nor_1 (Q, and_1_out, Q_prime);
  nor nor_2 (Q_prime, Q, and_2_out);
endmodule

module d_flip_flop (
  input  d,
  input  e,
  output q,
  output q_prime
);

  wire d_latch_1_q, not_1_out, not_2_out;

  d_latch d_latch_1 (.Q(d_latch_1_q), .\input (d), .enabler(not_1_out));  // open: Q_prime
  not not_1 (not_1_out, e);
  not not_2 (not_2_out, not_1_out);
  d_latch d_latch_2 (.Q(q), .Q_prime(q_prime), .\input (d_latch_1_q), .enabler(not_2_out));
endmodule

module full_adder_1_bit (
  input  input_1_1_bit,
  input  input_2_1_bit,
  input  carry_in,
  output carry_out,
  output result
);

  wire and_1_out, and_2_out, and_3_out, and_4_out, xor_1_out;

  ExactlyOne xor_1 (.out(xor_1_out), .in0(input_1_1_bit), .in1(input_2_1_bit), .in2(carry_in));
  and and_1 (and_1_out, input_1_1_bit, input_2_1_bit, carry_in);
  and and_2 (and_2_out, input_1_1_bit, input_2_1_bit);
  and and_3 (and_3_out, input_2_1_bit, carry_in);
  and and_4 (and_4_out, input_1_1_bit, carry_in);
  or or_1 (result, xor_1_out, and_1_out);
  or or_2 (carry_out, and_2_out, and_3_out, and_4_out);
endmodule

module full_adder_4_bit (
  input  [3:0] input1_4_bit,
  input  [3:0] input2_4_bit,
  input  carry_in,
  output carry_out,
  output [3:0] \output 
);

  wire full_adder_1_bit_2_carry_out, full_adder_1_bit_3_carry_out, full_adder_1_bit_4_carry_out;

  full_adder_1_bit full_adder_1_bit_1 (
    .input_1_1_bit(input1_4_bit[3]), .input_2_1_bit(input2_4_bit[3]),
    .carry_in(full_adder_1_bit_2_carry_out), .carry_out(carry_out), .result(\output [3]));
  full_adder_1_bit full_adder_1_bit_2 (
    .input_1_1_bit(input1_4_bit[2]), .input_2_1_bit(input2_4_bit[2]),
    .carry_in(full_adder_1_bit_3_carry_out), .carry_out(full_adder_1_bit_2_carry_out), .result(\output [2]));
  full_adder_1_bit full_adder_1_bit_3 (
    .input_1_1_bit(input1_4_bit[1]), .input_2_1_bit(input2_4_bit[1]),
    .carry_in(full_adder_1_bit_4_carry_out), .carry_out(full_adder_1_bit_3_carry_out), .result(\output [1]));
  full_adder_1_bit full_adder_1_bit_4 (
    .input_1_1_bit(input1_4_bit[0]), .input_2_1_bit(input2_4_bit[0]), .carry_in(carry_in),
    .carry_out(full_adder_1_bit_4_carry_out), .result(\output [0]));
endmodule

module full_adder_16_bit (
  input  [15:0] input_1_16_bit,
  input  [15:0] input__16_bit,
  input  carry_in,
  output carry_out,
  output [15:0] \output 
);

  wire full_adder_4_bit_2_carry_out, full_adder_4_bit_3_carry_out, full_adder_4_bit_4_carry_out;

  full_adder_4_bit full_adder_4_bit_1 (
    .input1_4_bit(input_1_16_bit[15:12]), .input2_4_bit(input__16_bit[15:12]),
    .carry_in(full_adder_4_bit_2_carry_out), .carry_out(carry_out), .\output (\output [15:12]));
  full_adder_4_bit full_adder_4_bit_2 (
    .input1_4_bit(input_1_16_bit[11:8]), .input2_4_bit(input__16_bit[11:8]),
    .carry_in(full_adder_4_bit_3_carry_out), .carry_out(full_adder_4_bit_2_carry_out),
    .\output (\output [11:8]));
  full_adder_4_bit full_adder_4_bit_3 (
    .input1_4_bit(input_1_16_bit[7:4]), .input2_4_bit(input__16_bit[7:4]),
    .carry_in(full_adder_4_bit_4_carry_out), .carry_out(full_adder_4_bit_3_carry_out),
    .\output (\output [7:4]));
  full_adder_4_bit full_adder_4_bit_4 (
    .input1_4_bit(input_1_16_bit[3:0]), .input2_4_bit(input__16_bit[3:0]), .carry_in(carry_in),
    .carry_out(full_adder_4_bit_4_carry_out), .\output (\output [3:0]));
endmodule

// Adder
module full_adder_18_bit (
  input  [17:0] input1,
  input  [17:0] input2,
  input  carry_in,
  output carry_out,
  output [17:0] out_5
);

  wire full_adder_1_bit_1_carry_out, full_adder_1_bit_2_carry_out;

  full_adder_16_bit full_adder_16_bit_1 (
    .input_1_16_bit(input1[17:2]), .input__16_bit(input2[17:2]), .carry_in(full_adder_1_bit_1_carry_out),
    .carry_out(carry_out), .\output (out_5[17:2]));
  full_adder_1_bit full_adder_1_bit_1 (
    .input_1_1_bit(input1[1]), .input_2_1_bit(input2[1]), .carry_in(full_adder_1_bit_2_carry_out),
    .carry_out(full_adder_1_bit_1_carry_out), .result(out_5[1]));
  full_adder_1_bit full_adder_1_bit_2 (
    .input_1_1_bit(input1[0]), .input_2_1_bit(input2[0]), .carry_in(carry_in),
    .carry_out(full_adder_1_bit_2_carry_out), .result(out_5[0]));
endmodule

// Reg
module register (
  input  [17:0] loadingBit,
  input  clock,
  input  [1:0] selectBit,
  output [17:0] outputBit
);

  wire [17:0] multiplexer_1_out;

  Multiplexer #(.select(2), .width(18), .enable("false")) multiplexer_1 (
    .in0(outputBit), .in1(loadingBit), .in2({18{1'b1}}), .in3({18{1'b0}}), .out(multiplexer_1_out),
    .sel(selectBit));
  d_flip_flop d_flip_flop_1 (.d(multiplexer_1_out[0]), .e(clock), .q(outputBit[0]));  // open: q_prime
  d_flip_flop d_flip_flop_2 (.d(multiplexer_1_out[1]), .e(clock), .q(outputBit[1]));  // open: q_prime
  d_flip_flop d_flip_flop_3 (.d(multiplexer_1_out[2]), .e(clock), .q(outputBit[2]));  // open: q_prime
  d_flip_flop d_flip_flop_4 (.d(multiplexer_1_out[3]), .e(clock), .q(outputBit[3]));  // open: q_prime
  d_flip_flop d_flip_flop_5 (.d(multiplexer_1_out[4]), .e(clock), .q(outputBit[4]));  // open: q_prime
  d_flip_flop d_flip_flop_6 (.d(multiplexer_1_out[5]), .e(clock), .q(outputBit[5]));  // open: q_prime
  d_flip_flop d_flip_flop_7 (.d(multiplexer_1_out[6]), .e(clock), .q(outputBit[6]));  // open: q_prime
  d_flip_flop d_flip_flop_8 (.d(multiplexer_1_out[7]), .e(clock), .q(outputBit[7]));  // open: q_prime
  d_flip_flop d_flip_flop_9 (.d(multiplexer_1_out[8]), .e(clock), .q(outputBit[8]));  // open: q_prime
  d_flip_flop d_flip_flop_10 (.d(multiplexer_1_out[9]), .e(clock), .q(outputBit[9]));  // open: q_prime
  d_flip_flop d_flip_flop_11 (.d(multiplexer_1_out[10]), .e(clock), .q(outputBit[10]));  // open: q_prime
  d_flip_flop d_flip_flop_12 (.d(multiplexer_1_out[11]), .e(clock), .q(outputBit[11]));  // open: q_prime
  d_flip_flop d_flip_flop_13 (.d(multiplexer_1_out[12]), .e(clock), .q(outputBit[12]));  // open: q_prime
  d_flip_flop d_flip_flop_14 (.d(multiplexer_1_out[13]), .e(clock), .q(outputBit[13]));  // open: q_prime
  d_flip_flop d_flip_flop_15 (.d(multiplexer_1_out[14]), .e(clock), .q(outputBit[14]));  // open: q_prime
  d_flip_flop d_flip_flop_16 (.d(multiplexer_1_out[15]), .e(clock), .q(outputBit[15]));  // open: q_prime
  d_flip_flop d_flip_flop_17 (.d(multiplexer_1_out[16]), .e(clock), .q(outputBit[16]));  // open: q_prime
  d_flip_flop d_flip_flop_18 (.d(multiplexer_1_out[17]), .e(clock), .q(outputBit[17]));  // open: q_prime

  // Notes on the sheet:
  //   00 - KEEP
  //   01- LOAD
  //   10 - SETTO(15)
  //   11 - SETTOZERO
endmodule

// RegisterList
module registerList (
  input  enableOutdata1,
  input  [4:0] read2,
  input  enableOutdata2,
  input  [4:0] read1,
  input  [17:0] inData1,
  input  [1:0] registerState,
  input  [4:0] write1,
  input  clock,
  output [17:0] outData2,
  output [17:0] outData1
);

  wire decoder_1_out0, decoder_1_out1, decoder_1_out2, decoder_1_out3, decoder_1_out4, decoder_1_out5,
       decoder_1_out6, decoder_1_out7, decoder_1_out8, decoder_1_out9, decoder_1_out10, decoder_1_out11,
       decoder_1_out12, decoder_1_out13, decoder_1_out14, decoder_1_out15, decoder_1_out16, decoder_1_out17,
       decoder_2_out0, decoder_2_out1, decoder_2_out2, decoder_2_out3, decoder_2_out4, decoder_2_out5,
       decoder_2_out6, decoder_2_out7, decoder_2_out8, decoder_2_out9, decoder_2_out10, decoder_2_out11,
       decoder_2_out12, decoder_2_out13, decoder_2_out14, decoder_2_out15, decoder_2_out16, decoder_2_out17,
       xor_1_out;
  wire [1:0] smallmux_1_output, smallmux_2_output, smallmux_3_output, smallmux_4_output, smallmux_5_output,
       smallmux_6_output, smallmux_7_output, smallmux_8_output, smallmux_9_output, smallmux_10_output,
       smallmux_11_output, smallmux_12_output, smallmux_13_output, smallmux_14_output, smallmux_15_output,
       smallmux_16_output, smallmux_17_output, smallmux_18_output, undriven, undriven_2, undriven_3,
       undriven_4, undriven_5, undriven_6, undriven_7, undriven_8, undriven_9, undriven_10, undriven_11,
       undriven_12, undriven_13, undriven_14, undriven_15, undriven_16, undriven_17, undriven_18;
  wire [17:0] register_1_outputbit, register_2_outputbit, register_3_outputbit, register_4_outputbit,
       register_5_outputbit, register_6_outputbit, register_7_outputbit, register_8_outputbit,
       register_9_outputbit, register_10_outputbit, register_11_outputbit, register_12_outputbit,
       register_13_outputbit, register_14_outputbit, register_15_outputbit, register_16_outputbit,
       register_17_outputbit, register_18_outputbit;

  Multiplexer #(.select(5), .width(2), .disabled(0), .enable("false")) multiplexer_1 (
    .in0(undriven), .in1(undriven_2), .in2(undriven_3), .in3(undriven_4), .in4(undriven_5), .in5(undriven_6),
    .in6(undriven_7), .in7(undriven_8), .in8(undriven_9), .in9(undriven_10), .in10(undriven_11),
    .in11(undriven_12), .in12(undriven_13), .in13(undriven_14), .in14(undriven_15), .in15(undriven_16),
    .in16(undriven_17), .in17(undriven_18), .out(registerState), .sel(write1));  // open: in18, in19, in20, in21, in22, in23, in24, in25, in26, in27, in28, in29, in30, in31
  smallMux smallmux_1 (.input1(registerState), .input2(undriven), .selectB(xor_1_out), .\output (smallmux_1_output));
  smallMux smallmux_2 (.input1(registerState), .input2(undriven_2), .selectB(xor_1_out), .\output (smallmux_2_output));
  smallMux smallmux_3 (.input1(registerState), .input2(undriven_3), .selectB(xor_1_out), .\output (smallmux_3_output));
  smallMux smallmux_4 (.input1(registerState), .input2(undriven_4), .selectB(xor_1_out), .\output (smallmux_4_output));
  smallMux smallmux_5 (.input1(registerState), .input2(undriven_5), .selectB(xor_1_out), .\output (smallmux_5_output));
  smallMux smallmux_6 (.input1(registerState), .input2(undriven_6), .selectB(xor_1_out), .\output (smallmux_6_output));
  smallMux smallmux_7 (.input1(registerState), .input2(undriven_7), .selectB(xor_1_out), .\output (smallmux_7_output));
  smallMux smallmux_8 (.input1(registerState), .input2(undriven_8), .selectB(xor_1_out), .\output (smallmux_8_output));
  smallMux smallmux_9 (.input1(registerState), .input2(undriven_9), .selectB(xor_1_out), .\output (smallmux_9_output));
  smallMux smallmux_10 (
    .input1(registerState), .input2(undriven_10), .selectB(xor_1_out), .\output (smallmux_10_output));
  smallMux smallmux_11 (
    .input1(registerState), .input2(undriven_11), .selectB(xor_1_out), .\output (smallmux_11_output));
  smallMux smallmux_12 (
    .input1(registerState), .input2(undriven_12), .selectB(xor_1_out), .\output (smallmux_12_output));
  smallMux smallmux_13 (
    .input1(registerState), .input2(undriven_13), .selectB(xor_1_out), .\output (smallmux_13_output));
  smallMux smallmux_14 (
    .input1(registerState), .input2(undriven_14), .selectB(xor_1_out), .\output (smallmux_14_output));
  smallMux smallmux_15 (
    .input1(registerState), .input2(undriven_15), .selectB(xor_1_out), .\output (smallmux_15_output));
  smallMux smallmux_16 (
    .input1(registerState), .input2(undriven_16), .selectB(xor_1_out), .\output (smallmux_16_output));
  smallMux smallmux_17 (
    .input1(registerState), .input2(undriven_17), .selectB(xor_1_out), .\output (smallmux_17_output));
  smallMux smallmux_18 (
    .input1(registerState), .input2(undriven_18), .selectB(xor_1_out), .\output (smallmux_18_output));
  Decoder #(.select(5), .disabled(0)) decoder_1 (
    .out0(decoder_1_out0), .out1(decoder_1_out1), .out2(decoder_1_out2), .out3(decoder_1_out3),
    .out4(decoder_1_out4), .out5(decoder_1_out5), .out6(decoder_1_out6), .out7(decoder_1_out7),
    .out8(decoder_1_out8), .out9(decoder_1_out9), .out10(decoder_1_out10), .out11(decoder_1_out11),
    .out12(decoder_1_out12), .out13(decoder_1_out13), .out14(decoder_1_out14), .out15(decoder_1_out15),
    .out16(decoder_1_out16), .out17(decoder_1_out17), .sel(read2), .en(enableOutdata1));  // open: out18, out19, out20, out21, out22, out23, out24, out25, out26, out27, out28, out29, out30, out31
  xor xor_1 (xor_1_out, registerState[0], registerState[1]);
  register register_1 (
    .loadingBit(inData1), .clock(clock), .selectBit(smallmux_1_output), .outputBit(register_1_outputbit));
  register register_2 (
    .loadingBit(inData1), .clock(clock), .selectBit(smallmux_2_output), .outputBit(register_2_outputbit));
  register register_3 (
    .loadingBit(inData1), .clock(clock), .selectBit(smallmux_3_output), .outputBit(register_3_outputbit));
  register register_4 (
    .loadingBit(inData1), .clock(clock), .selectBit(smallmux_4_output), .outputBit(register_4_outputbit));
  register register_5 (
    .loadingBit(inData1), .clock(clock), .selectBit(smallmux_5_output), .outputBit(register_5_outputbit));
  register register_6 (
    .loadingBit(inData1), .clock(clock), .selectBit(smallmux_6_output), .outputBit(register_6_outputbit));
  register register_7 (
    .loadingBit(inData1), .clock(clock), .selectBit(smallmux_7_output), .outputBit(register_7_outputbit));
  register register_8 (
    .loadingBit(inData1), .clock(clock), .selectBit(smallmux_8_output), .outputBit(register_8_outputbit));
  register register_9 (
    .loadingBit(inData1), .clock(clock), .selectBit(smallmux_9_output), .outputBit(register_9_outputbit));
  register register_10 (
    .loadingBit(inData1), .clock(clock), .selectBit(smallmux_10_output), .outputBit(register_10_outputbit));
  register register_11 (
    .loadingBit(inData1), .clock(clock), .selectBit(smallmux_11_output), .outputBit(register_11_outputbit));
  register register_12 (
    .loadingBit(inData1), .clock(clock), .selectBit(smallmux_12_output), .outputBit(register_12_outputbit));
  register register_13 (
    .loadingBit(inData1), .clock(clock), .selectBit(smallmux_13_output), .outputBit(register_13_outputbit));
  register register_14 (
    .loadingBit(inData1), .clock(clock), .selectBit(smallmux_14_output), .outputBit(register_14_outputbit));
  register register_15 (
    .loadingBit(inData1), .clock(clock), .selectBit(smallmux_15_output), .outputBit(register_15_outputbit));
  register register_16 (
    .loadingBit(inData1), .clock(clock), .selectBit(smallmux_16_output), .outputBit(register_16_outputbit));
  register register_17 (
    .loadingBit(inData1), .clock(clock), .selectBit(smallmux_17_output), .outputBit(register_17_outputbit));
  register register_18 (
    .loadingBit(inData1), .clock(clock), .selectBit(smallmux_18_output), .outputBit(register_18_outputbit));
  Clock clock_1 ();  // open: out
  assign outData2 = decoder_2_out0 ? register_1_outputbit : 18'bz;  // Controlled_Buffer controlled_buffer_1
  assign outData1 = decoder_1_out0 ? register_1_outputbit : 18'bz;  // Controlled_Buffer controlled_buffer_2
  assign outData2 = decoder_2_out1 ? register_2_outputbit : 18'bz;  // Controlled_Buffer controlled_buffer_3
  assign outData1 = decoder_1_out1 ? register_2_outputbit : 18'bz;  // Controlled_Buffer controlled_buffer_4
  assign outData2 = decoder_2_out2 ? register_3_outputbit : 18'bz;  // Controlled_Buffer controlled_buffer_5
  assign outData1 = decoder_1_out2 ? register_3_outputbit : 18'bz;  // Controlled_Buffer controlled_buffer_6
  assign outData2 = decoder_2_out3 ? register_4_outputbit : 18'bz;  // Controlled_Buffer controlled_buffer_7
  assign outData1 = decoder_1_out3 ? register_4_outputbit : 18'bz;  // Controlled_Buffer controlled_buffer_8
  assign outData2 = decoder_2_out4 ? register_5_outputbit : 18'bz;  // Controlled_Buffer controlled_buffer_9
  assign outData1 = decoder_1_out4 ? register_5_outputbit : 18'bz;  // Controlled_Buffer controlled_buffer_10
  assign outData2 = decoder_2_out5 ? register_6_outputbit : 18'bz;  // Controlled_Buffer controlled_buffer_11
  assign outData1 = decoder_1_out5 ? register_6_outputbit : 18'bz;  // Controlled_Buffer controlled_buffer_12
  assign outData2 = decoder_2_out6 ? register_7_outputbit : 18'bz;  // Controlled_Buffer controlled_buffer_13
  assign outData1 = decoder_1_out6 ? register_7_outputbit : 18'bz;  // Controlled_Buffer controlled_buffer_14
  assign outData2 = decoder_2_out7 ? register_8_outputbit : 18'bz;  // Controlled_Buffer controlled_buffer_15
  assign outData1 = decoder_1_out7 ? register_8_outputbit : 18'bz;  // Controlled_Buffer controlled_buffer_16
  assign outData2 = decoder_2_out8 ? register_9_outputbit : 18'bz;  // Controlled_Buffer controlled_buffer_17
  assign outData1 = decoder_1_out8 ? register_9_outputbit : 18'bz;  // Controlled_Buffer controlled_buffer_18
  assign outData2 = decoder_2_out9 ? register_10_outputbit : 18'bz;  // Controlled_Buffer controlled_buffer_19
  assign outData1 = decoder_1_out9 ? register_10_outputbit : 18'bz;  // Controlled_Buffer controlled_buffer_20
  assign outData2 = decoder_2_out10 ? register_11_outputbit : 18'bz;  // Controlled_Buffer controlled_buffer_21
  assign outData1 = decoder_1_out10 ? register_11_outputbit : 18'bz;  // Controlled_Buffer controlled_buffer_22
  assign outData2 = decoder_2_out11 ? register_12_outputbit : 18'bz;  // Controlled_Buffer controlled_buffer_23
  assign outData1 = decoder_1_out11 ? register_12_outputbit : 18'bz;  // Controlled_Buffer controlled_buffer_24
  assign outData2 = decoder_2_out12 ? register_13_outputbit : 18'bz;  // Controlled_Buffer controlled_buffer_25
  assign outData1 = decoder_1_out12 ? register_13_outputbit : 18'bz;  // Controlled_Buffer controlled_buffer_26
  assign outData2 = decoder_2_out14 ? register_14_outputbit : 18'bz;  // Controlled_Buffer controlled_buffer_27
  assign outData1 = decoder_1_out13 ? register_14_outputbit : 18'bz;  // Controlled_Buffer controlled_buffer_28
  assign outData2 = decoder_2_out13 ? register_15_outputbit : 18'bz;  // Controlled_Buffer controlled_buffer_29
  assign outData1 = decoder_1_out14 ? register_15_outputbit : 18'bz;  // Controlled_Buffer controlled_buffer_30
  assign outData2 = decoder_2_out15 ? register_16_outputbit : 18'bz;  // Controlled_Buffer controlled_buffer_31
  assign outData1 = decoder_1_out15 ? register_16_outputbit : 18'bz;  // Controlled_Buffer controlled_buffer_32
  assign outData2 = decoder_2_out16 ? register_17_outputbit : 18'bz;  // Controlled_Buffer controlled_buffer_33
  assign outData1 = decoder_1_out16 ? register_17_outputbit : 18'bz;  // Controlled_Buffer controlled_buffer_34
  assign outData2 = decoder_2_out17 ? register_18_outputbit : 18'bz;  // Controlled_Buffer controlled_buffer_35
  assign outData1 = decoder_1_out17 ? register_18_outputbit : 18'bz;  // Controlled_Buffer controlled_buffer_36
  Decoder #(.select(5), .disabled(0)) decoder_2 (
    .out0(decoder_2_out0), .out1(decoder_2_out1), .out2(decoder_2_out2), .out3(decoder_2_out3),
    .out4(decoder_2_out4), .out5(decoder_2_out5), .out6(decoder_2_out6), .out7(decoder_2_out7),
    .out8(decoder_2_out8), .out9(decoder_2_out9), .out10(decoder_2_out10), .out11(decoder_2_out11),
    .out12(decoder_2_out12), .out13(decoder_2_out13), .out14(decoder_2_out14), .out15(decoder_2_out15),
    .out16(decoder_2_out16), .out17(decoder_2_out17), .sel(read1), .en(enableOutdata2));  // open: out18, out19, out20, out21, out22, out23, out24, out25, out26, out27, out28, out29, out30, out31

  // Notes on the sheet:
  //   For states 00(keep) and 11(set to zero)
  //   Ters olmuşlar :)
  //   Düzelttim
endmodule

// ALU
module alu (
  input  enable_bit,
  input  [1:0] selection_bit_1,
  input  [17:0] input_1_18_bit,
  input  isCMP,
  input  [17:0] input_2_18_bit,
  output [17:0] \output ,
  output ZF,
  output CF
);

  wire not_1_out;
  wire [17:0] and_1_out, controlled_buffer_1_out, demultiplexer_1_out0, demultiplexer_1_out1,
       demultiplexer_1_out2, demultiplexer_1_out3, demultiplexer_2_out0, demultiplexer_2_out1,
       demultiplexer_2_out2, demultiplexer_2_out3, full_adder_18_bit_1_out_5, multiplexer_1_out,
       multiplexer_2_out, nand_1_out, nor_1_out, not_2_out;

  isEqual isequal_1 (.input2({18{1'b0}}), .input1(controlled_buffer_1_out), .\output (ZF));
  not not_1 (not_1_out, isCMP);
  getSignBit getsignbit_1 (.\input (controlled_buffer_1_out), .signBit(CF));
  assign not_2_out = ~demultiplexer_2_out0;  // NOT_Gate not_2, 18 bits wide
  Multiplexer #(.width(18), .enable("false")) multiplexer_1 (
    .in0(demultiplexer_2_out0), .in1(not_2_out), .out(multiplexer_1_out), .sel(isCMP));
  full_adder_18_bit full_adder_18_bit_1 (
    .input1(demultiplexer_1_out0), .input2(multiplexer_1_out), .carry_in(isCMP),
    .out_5(full_adder_18_bit_1_out_5));  // open: carry_out
  assign controlled_buffer_1_out = isCMP ? multiplexer_2_out : 18'bz;  // Controlled_Buffer controlled_buffer_1
  Demultiplexer #(.select(2), .width(18)) demultiplexer_1 (
    .out0(demultiplexer_1_out0), .out1(demultiplexer_1_out1), .out2(demultiplexer_1_out2),
    .out3(demultiplexer_1_out3), .in(input_1_18_bit), .sel(selection_bit_1), .en(enable_bit));
  assign and_1_out = demultiplexer_2_out1 & demultiplexer_1_out1;  // AND_Gate and_1, 18 bits wide
  Demultiplexer #(.select(2), .width(18)) demultiplexer_2 (
    .out0(demultiplexer_2_out0), .out1(demultiplexer_2_out1), .out2(demultiplexer_2_out2),
    .out3(demultiplexer_2_out3), .in(input_2_18_bit), .sel(selection_bit_1), .en(enable_bit));
  assign nor_1_out = ~(demultiplexer_2_out2 | demultiplexer_1_out2);  // NOR_Gate nor_1, 18 bits wide
  assign \output  = not_1_out ? multiplexer_2_out : 18'bz;  // Controlled_Buffer controlled_buffer_2
  assign nand_1_out = ~(demultiplexer_2_out3 & demultiplexer_1_out3);  // NAND_Gate nand_1, 18 bits wide
  Multiplexer #(.select(2), .width(18)) multiplexer_2 (
    .in0(full_adder_18_bit_1_out_5), .in1(and_1_out), .in2(nor_1_out), .in3(nand_1_out),
    .out(multiplexer_2_out), .sel(selection_bit_1), .en(enable_bit));

  // Notes on the sheet:
  //   input1-input2
  //   AND = 01
  //   ADD = 00
  //   NAND = 10
  //   NOR = 11
endmodule

module _1__0_sequential (
  input  clock,
  output out_2
);

  Multiplexer #(.disabled(0)) multiplexer_1 (.in0(1'b1), .in1(1'b0), .out(out_2), .sel(clock), .en(out_2));
endmodule

// PC
module Program_Counter (
  input  incrementPC,
  input  [17:0] Jump_value,
  input  Jump_enable,
  input  setToZero,
  input  Clock,
  output [17:0] PC_value
);

  wire [1:0] smallmux_1_output;
  wire [17:0] full_adder_18_bit_1_out_5, full_adder_18_bit_2_out_5, multiplexer_1_out,
       n10_18_sign_extender_1__18_bit_output;

  _10__18_sign_extender u_10_18_sign_extender_1 (
    ._10_bit_input(Jump_value[9:0]), ._18_bit_output(n10_18_sign_extender_1__18_bit_output));
  smallMux smallmux_1 (.input1(2'b01), .input2(2'b11), .selectB(setToZero), .\output (smallmux_1_output));
  full_adder_18_bit full_adder_18_bit_1 (
    .input1(PC_value), .input2({{17{1'b0}}, incrementPC}), .carry_in(1'b0), .out_5(full_adder_18_bit_1_out_5));  // open: carry_out
  full_adder_18_bit full_adder_18_bit_2 (
    .input1(PC_value), .input2(n10_18_sign_extender_1__18_bit_output), .carry_in(1'b0),
    .out_5(full_adder_18_bit_2_out_5));  // open: carry_out
  Multiplexer #(.width(18), .enable("false")) multiplexer_1 (
    .in0(full_adder_18_bit_1_out_5), .in1(full_adder_18_bit_2_out_5), .out(multiplexer_1_out),
    .sel(Jump_enable));
  register register_1 (
    .loadingBit(multiplexer_1_out), .clock(Clock), .selectBit(smallmux_1_output), .outputBit(PC_value));

  // Notes on the sheet:
  //   Start adress
endmodule

module Jumps (
  input  CF,
  input  ZF,
  input  Enable_from_control_unit,
  input  [2:0] Jump_selector,
  output Jump_enable
);

  wire and_1_out, and_2_out, and_3_out, and_4_out, and_5_out, decoder_1_out0, decoder_1_out1, decoder_1_out2,
       decoder_1_out3, decoder_1_out4, decoder_1_out5, not_1_out, not_2_out, or_1_out;

  Decoder #(.select(3), .enable("false")) decoder_1 (
    .out0(decoder_1_out0), .out1(decoder_1_out1), .out2(decoder_1_out2), .out3(decoder_1_out3),
    .out4(decoder_1_out4), .out5(decoder_1_out5), .sel(Jump_selector));  // open: out6, out7
  not not_1 (not_1_out, CF);
  not not_2 (not_2_out, ZF);
  and and_1 (and_1_out, not_1_out, decoder_1_out0, ZF);
  and and_2 (and_2_out, not_1_out, decoder_1_out1, not_2_out);
  and and_3 (and_3_out, CF, decoder_1_out2, not_2_out);
  and and_4 (and_4_out, decoder_1_out3, not_1_out);
  and and_5 (and_5_out, CF, decoder_1_out4, ZF);
  or or_1 (or_1_out, and_1_out, and_2_out, and_3_out, and_4_out, and_5_out, decoder_1_out5);
  and and_6 (Jump_enable, or_1_out, Enable_from_control_unit);

  // Notes on the sheet:
  //   JE = 000
  //   JA = 001
  //   JB = 010
  //   JAE = 011
  //   JBE = 100
  //   JUMP = 101
  //   JE
  //   JA
  //   JB
endmodule

module isEqual (
  input  [17:0] input2,
  input  [17:0] input1,
  output \output 
);

  wire or_1_out;
  wire [17:0] xor_1_out;

  assign xor_1_out = input2 ^ input1;  // XOR_Gate xor_1, 18 bits wide
  or or_1 (or_1_out, xor_1_out[17], xor_1_out[16], xor_1_out[15], xor_1_out[14], xor_1_out[13], xor_1_out[12], xor_1_out[11], xor_1_out[10], xor_1_out[9], xor_1_out[8], xor_1_out[7], xor_1_out[6], xor_1_out[5], xor_1_out[4], xor_1_out[3], xor_1_out[2], xor_1_out[1], xor_1_out[0]);
  not not_1 (\output , or_1_out);
endmodule

module getSignBit (
  input  [17:0] \input ,
  output signBit
);


  assign signBit = \input [17];
endmodule

module main (
  input  in_1
);

  wire ALUEnable, CFInput, CFOutput, IncrementPC, instructionReadEnable, isCMP, isIMM, jumpEnable,
       Jumps_enable, LDEnable, RegisterRead1Enable, RegisterRead2Enable, setRegisterToZero, STEnable,
       ZFInput, ZFOutput;
  wire [1:0] ALUSelectionBits, RegisterState;
  wire [2:0] Jump_selector;
  wire [4:0] RegisterRead1SelectBit, RegisterRead2SelectBit, RegisterWrite1SelectBit;
  wire [9:0] sign_ext__10_bit_output;
  wire [17:0] alu_1_output, instructionInput, multiplexer_1_out, multiplexer_2_out,
       program_counter_1_pc_value, ram_1_data, registerlist_1_outdata1, registerlist_1_outdata2,
       sign_ext_2_out_2;

  _18__10_sign_extender sign_ext (._18_bit_input(program_counter_1_pc_value), ._10_bit_output(sign_ext__10_bit_output));
  Program_Counter program_counter_1 (
    .incrementPC(IncrementPC), .Jump_value(instructionInput), .Jump_enable(jumpEnable),
    .setToZero(setRegisterToZero), .Clock(in_1), .PC_value(program_counter_1_pc_value));
  ControlCircuit controlcircuit_1 (
    .instruction_in(instructionInput), .Clock(in_1), .jump_enable_for_jumps_to_control(Jumps_enable),
    .jump_selector(Jump_selector), .alu_enable(ALUEnable), .ALU_selector(ALUSelectionBits),
    .setRegisterEmpty(setRegisterToZero), .incrementCMP(IncrementPC),
    .readInstruction(instructionReadEnable), .registerState(RegisterState), .CMPEnable(isCMP),
    .LDEnable(LDEnable), .STEnable(STEnable), .isIMM(isIMM));  // open: sn_out
  ROM #(.addrWidth(10), .dataWidth(18)) rom_1 (.addr(sign_ext__10_bit_output), .data(instructionInput), .sel(1'b1));
  flagRegister ZF (
    .readEnable(jumpEnable), .inputData(ZFInput), .setToZero(setRegisterToZero), .clock(in_1),
    .writeEnable(isCMP), .outputBit(ZFOutput));
  Jumps Jumps (
    .CF(CFOutput), .ZF(ZFOutput), .Enable_from_control_unit(Jumps_enable), .Jump_selector(Jump_selector),
    .Jump_enable(jumpEnable));
  flagRegister flagregister_1 (
    .readEnable(jumpEnable), .inputData(CFInput), .setToZero(setRegisterToZero), .clock(in_1),
    .writeEnable(isCMP), .outputBit(CFOutput));
  _6__18_sign_extender sign_ext_2 (.in_1(instructionInput[5:0]), .out_2(sign_ext_2_out_2));
  registerList registerlist_1 (
    .enableOutdata1(RegisterRead1Enable), .read2(RegisterRead2SelectBit),
    .enableOutdata2(RegisterRead2Enable), .read1(RegisterRead1SelectBit), .inData1(multiplexer_2_out),
    .registerState(RegisterState), .write1(RegisterWrite1SelectBit), .clock(in_1),
    .outData2(registerlist_1_outdata2), .outData1(registerlist_1_outdata1));
  Multiplexer #(.width(18), .enable("false")) multiplexer_1 (
    .in0(registerlist_1_outdata2), .in1(sign_ext_2_out_2), .out(multiplexer_1_out), .sel(isIMM));
  alu alu_1 (
    .input_1_18_bit(registerlist_1_outdata1), .selection_bit_1(ALUSelectionBits), .enable_bit(ALUEnable),
    .\output (alu_1_output), .isCMP(isCMP), .ZF(ZFInput), .CF(CFInput), .input_2_18_bit(multiplexer_1_out));
  Multiplexer #(.width(18), .enable("false")) multiplexer_2 (
    .in0(ram_1_data), .in1(alu_1_output), .out(multiplexer_2_out), .sel(ALUEnable));
  RAM #(.addrWidth(10), .dataWidth(18), .bus("separate")) ram_1 (
    .addr(instructionInput[17:8]), .din(registerlist_1_outdata1), .data(ram_1_data), .str(STEnable),
    .sel(1'b1), .clk(in_1), .ld(LDEnable), .clr(1'b0));

  // Other names for the same wires on the sheet: clock = in_1

  // Notes on the sheet:
  //   Controller input(s)/output(s)
  //   InstructionMemory
  //   contents of rom_1 (hex, n*v repeats v):
  //   1c001 1c002 1c064 1c3ff 1c200 2c3ff 2c000 2c064 2c3ff 2c200 303ff 30000 30064 303ff 30200 343ff
  //   34000 34064 343ff 34200 383ff 38000 38064 383ff 38200 3c3ff 3c000 3c064 3c3ff 3c200 203ff 23c00
  //   22464 243ff 27c00 26464 28402 2800f 29c0a 2b005
  //   CF
  //   RAM
endmodule

module flagRegister (
  input  readEnable,
  input  inputData,
  input  setToZero,
  input  clock,
  input  writeEnable,
  output outputBit
);

  wire and_1_out, and_2_out, d_flip_flop_1_q, multiplexer_1_out, or_2_out;
  wire [0:0] or_1_out;

  Multiplexer #(.select(2), .enable("false")) multiplexer_1 (
    .in0(d_flip_flop_1_q), .in1(inputData), .in2(1'b1), .in3(1'b0), .out(multiplexer_1_out),
    .sel({setToZero, or_1_out[0]}));
  and and_1 (and_1_out, setToZero, clock);
  and and_2 (and_2_out, clock, writeEnable);
  or or_1 (or_1_out[0], writeEnable, setToZero);
  or or_2 (or_2_out, and_1_out, and_2_out);
  d_flip_flop d_flip_flop_1 (.d(multiplexer_1_out), .e(or_2_out), .q(d_flip_flop_1_q));  // open: q_prime
  assign outputBit = readEnable ? d_flip_flop_1_q : 1'bz;  // Controlled_Buffer controlled_buffer_1

  // Notes on the sheet:
  //   00 - KEEP
  //   01- LOAD
  //   10 - SETTO(15)
  //   11 - SETTOZERO
endmodule

module smallMux (
  input  [1:0] input1,
  input  [1:0] input2,
  input  selectB,
  output [1:0] \output 
);

  Multiplexer #(.width(2), .enable("false")) multiplexer_1 (.in0(input1), .in1(input2), .out(\output ), .sel(selectB));
endmodule

module ControlCircuit (
  input  [17:0] instruction_in,
  input  Clock,
  output [4:0] sn_out,
  output setRegisterEmpty,
  output jump_enable_for_jumps_to_control,
  output incrementCMP,
  output [1:0] registerState,
  output readInstruction,
  output CMPEnable,
  output LDEnable,
  output STEnable,
  output [2:0] jump_selector,
  output alu_enable,
  output [1:0] ALU_selector,
  output isIMM
);

  wire ADD_out, ADDI_out, AND_out, ANDI_out, JA_out, JAE_out, JB_out, JBE_out, JE_out, JUMP_out,
       n1_0_sequential_1_out_2, NAND_out, NOR_out, or_3_out, or_4_out, or_5_out;
  wire [4:0] controlcircuitstatelogic_1_out_3;
  wire [17:0] multiplexer_1_out;
  wire [17:5] register_1_outputbit;

  ControlCircuitStateLogic controlcircuitstatelogic_1 (
    .sn_in({sn_out[4:2], sn_out[2], sn_out[0]}), .instruction_in(instruction_in[17:14]),
    .out_3(controlcircuitstatelogic_1_out_3));
  and START (registerState[1], ~sn_out[0], ~sn_out[2], ~sn_out[2], ~sn_out[3], ~sn_out[4]);  // AND_Gate
  and FETCH1 (incrementCMP, sn_out[0], ~sn_out[2], ~sn_out[2], ~sn_out[3], ~sn_out[4]);  // AND_Gate
  and FETCH2 (readInstruction, sn_out[0], ~sn_out[2], ~sn_out[2], ~sn_out[3], sn_out[4]);  // AND_Gate
  and CMP (CMPEnable, ~sn_out[0], sn_out[2], ~sn_out[2], sn_out[3], ~sn_out[4]);  // AND_Gate
  and LD (LDEnable, ~sn_out[0], sn_out[2], ~sn_out[2], ~sn_out[3], ~sn_out[4]);  // AND_Gate
  and ST (STEnable, ~sn_out[0], sn_out[2], ~sn_out[2], ~sn_out[3], sn_out[4]);  // AND_Gate
  and JUMP (JUMP_out, ~sn_out[4], ~sn_out[3], sn_out[2], sn_out[2], sn_out[0]);  // AND_Gate
  and JE (JE_out, ~sn_out[4], sn_out[3], ~sn_out[2], sn_out[2], sn_out[0]);  // AND_Gate
  and JA (JA_out, ~sn_out[4], sn_out[3], sn_out[2], ~sn_out[2], ~sn_out[0]);  // AND_Gate
  and JB (JB_out, ~sn_out[4], sn_out[3], sn_out[2], ~sn_out[2], sn_out[0]);  // AND_Gate
  and JAE (JAE_out, ~sn_out[4], sn_out[3], sn_out[2], sn_out[2], ~sn_out[0]);  // AND_Gate
  and JBE (JBE_out, ~sn_out[4], sn_out[3], sn_out[2], sn_out[2], sn_out[0]);  // AND_Gate
  and ADD (ADD_out, ~sn_out[4], ~sn_out[3], ~sn_out[2], ~sn_out[2], sn_out[0]);  // AND_Gate
  and AND (AND_out, ~sn_out[4], ~sn_out[3], ~sn_out[2], sn_out[2], sn_out[0]);  // AND_Gate
  and NAND (NAND_out, ~sn_out[4], ~sn_out[3], sn_out[2], ~sn_out[2], sn_out[0]);  // AND_Gate
  and NOR (NOR_out, ~sn_out[4], ~sn_out[3], sn_out[2], sn_out[2], ~sn_out[0]);  // AND_Gate
  and ADDI (ADDI_out, ~sn_out[0], ~sn_out[2], ~sn_out[2], sn_out[3], ~sn_out[4]);  // AND_Gate
  and ANDI (ANDI_out, ~sn_out[0], ~sn_out[2], sn_out[2], ~sn_out[3], ~sn_out[4]);  // AND_Gate
  or or_1 (alu_enable, ANDI_out, ADD_out, AND_out, NAND_out, NOR_out, ADDI_out);
  assign jump_selector = JUMP_out ? 3'b101 : 3'bz;  // Controlled_Buffer controlled_buffer_1
  or or_2 (jump_enable_for_jumps_to_control, JUMP_out, JE_out, JA_out, JB_out, JAE_out, JBE_out);
  assign jump_selector = JE_out ? 3'b000 : 3'bz;  // Controlled_Buffer controlled_buffer_2
  assign jump_selector = JA_out ? 3'b001 : 3'bz;  // Controlled_Buffer controlled_buffer_3
  assign jump_selector = JB_out ? 3'b010 : 3'bz;  // Controlled_Buffer controlled_buffer_4
  assign jump_selector = JAE_out ? 3'b011 : 3'bz;  // Controlled_Buffer controlled_buffer_5
  assign jump_selector = JBE_out ? 3'b100 : 3'bz;  // Controlled_Buffer controlled_buffer_6
  or or_3 (or_3_out, ADD_out, ADDI_out);
  or or_4 (or_4_out, AND_out, ANDI_out);
  Multiplexer #(.width(18), .enable("false")) multiplexer_1 (
    .in0({{13{1'b1}}, controlcircuitstatelogic_1_out_3}), .in1({18{1'b0}}), .out(multiplexer_1_out),
    .sel(n1_0_sequential_1_out_2));
  or or_5 (or_5_out, LDEnable, alu_enable);
  assign ALU_selector = or_3_out ? 2'b00 : 2'bz;  // Controlled_Buffer controlled_buffer_7
  assign ALU_selector = or_4_out ? 2'b01 : 2'bz;  // Controlled_Buffer controlled_buffer_8
  assign ALU_selector = NAND_out ? 2'b10 : 2'bz;  // Controlled_Buffer controlled_buffer_9
  assign ALU_selector = NOR_out ? 2'b11 : 2'bz;  // Controlled_Buffer controlled_buffer_10
  _1__0_sequential u_1_0_sequential_1 (.clock(Clock), .out_2(n1_0_sequential_1_out_2));
  or or_6 (isIMM, ADDI_out, ANDI_out);
  register register_1 (
    .loadingBit(multiplexer_1_out), .clock(Clock), .selectBit(2'b01),
    .outputBit({register_1_outputbit, sn_out[4:2], sn_out[2], sn_out[0]}));
  or or_7 (registerState[0], registerState[1], or_5_out);

  assign setRegisterEmpty = registerState[1];
  assign sn_out[1] = sn_out[2];

  // Notes on the sheet:
  //   Start state
  //   will be connect to jumps
  //   will be connect to jumps
endmodule

module ControlCircuitStateLogic (
  input  [4:0] sn_in,
  input  [3:0] instruction_in,
  output [4:0] out_3
);

  wire and_1_out, and_2_out, and_3_out, and_4_out, and_5_out, not_1_out, not_2_out, or_1_out;

  and and_1 (and_1_out, ~instruction_in[0], ~instruction_in[1], ~instruction_in[2], ~instruction_in[3]);  // AND_Gate
  and and_2 (and_2_out, ~sn_in[0], ~sn_in[1], ~sn_in[2], ~sn_in[3], sn_in[4]);  // AND_Gate
  and and_3 (and_3_out, sn_in[0], ~sn_in[1], ~sn_in[2], ~sn_in[3], sn_in[4]);  // AND_Gate
  not not_1 (not_1_out, and_1_out);
  and and_4 (and_4_out, and_3_out, not_1_out);
  and and_5 (and_5_out, and_3_out, and_1_out);
  assign out_3 = and_2_out ? 5'b10001 : 5'bz;  // Controlled_Buffer controlled_buffer_1
  assign out_3 = and_4_out ? {1'b0, instruction_in} : 5'bz;  // Controlled_Buffer controlled_buffer_2
  assign out_3 = and_5_out ? 5'b10000 : 5'bz;  // Controlled_Buffer controlled_buffer_3
  not not_2 (not_2_out, or_1_out);
  or or_1 (or_1_out, and_2_out, and_4_out, and_5_out);
  assign out_3 = not_2_out ? 5'b10000 : 5'bz;  // Controlled_Buffer controlled_buffer_4

  // Notes on the sheet:
  //   10000 case
  //   10001 case
endmodule

module _18__10_sign_extender (
  input  [17:0] _18_bit_input,
  output [9:0] _10_bit_output
);


  assign _10_bit_output = _18_bit_input[9:0];
endmodule

module _6__18_sign_extender (
  input  [5:0] in_1,
  output [17:0] out_2
);


  assign out_2 = {{13{in_1[5]}}, in_1[4:0]};
endmodule

module _10__18_sign_extender (
  input  [9:0] _10_bit_input,
  output [17:0] _18_bit_output
);


  assign _18_bit_output = {{9{_10_bit_input[9]}}, _10_bit_input[8:0]};
endmodule
