// Logisim project d latch.circ as structural Verilog: 2 circuits, main circuit d-latch
module d_latch (
  input  D,
  input  enable,
  output Q,
  output Q_prime
);

  wire nand_1_out, nand_2_out, nand_3_out, nand_4_out, not_1_out;

  nand nand_1 (nand_1_out, D, enable);
  not not_1 (not_1_out, enable);
  nand nand_2 (nand_2_out, nand_1_out, not_1_out);
  nand nand_3 (nand_3_out, nand_1_out, nand_4_out);
  nand nand_4 (nand_4_out, nand_3_out, nand_2_out);
endmodule

module d_flip_flop (
  input  d,
  output q,
  output q_prime
);

  wire clock_1_out, d_latch_1_q_prime, d_latch_2_q_prime, not_1_out, undriven;

  Clock clock_1 (.out(clock_1_out));
  not not_1 (not_1_out, clock_1_out);
  d_latch d_latch_1 (.D(d), .Q(not_1_out), .Q_prime(d_latch_1_q_prime));  // open: enable
  d_latch d_latch_2 (.D(d_latch_1_q_prime), .Q(not_1_out), .Q_prime(d_latch_2_q_prime), .enable(undriven));
endmodule
